// Logisim project TRABALHO DE ARQUITETURA DE COMPUTADORES CC3MB.circ as structural Verilog: 5 circuits, main circuit main
module main (
  input  [3:0] in_1,
  input  [3:0] in_2,
  input  in_3,
  input  in_4,
  input  in_5,
  input  in_6,
  input  in_7,
  input  in_8,
  input  [3:0] in_9,
  input  [3:0] in_10,
  input  in_11,
  input  in_12,
  output out_13,
  output out_14,
  output out_15,
  output [3:0] out_16,
  output out_17,
  output out_18,
  output out_19,
  output [3:0] out_20
);

  ADD_1 add_1_1 (.A(in_3), .B(in_4), .VEM_1(in_5), .S(out_15), .VAI_1(out_13));
  Sub_1 sub_1_1 (.A(in_7), .B(in_8), .VEM_1(in_11), .S(out_19), .VAI_1(out_17));
  ADD_4 add_4_1 (.in_1(in_1), .VAI_1(out_14), .in_2(in_2), .VEM_1(in_6), .out_5(out_16));
  Sub_4 sub_4_1 (.Overflow(out_18), .in_1(in_9), .in_2(in_10), .Vem_1(in_12), .out_5(out_20));
endmodule

module ADD_1 (
  input  A,
  input  B,
  input  VEM_1,
  output S,
  output VAI_1
);

  wire and_1_out, and_2_out, or_1_out, xor_1_out;

  xor xor_1 (xor_1_out, A, B);
  or or_1 (or_1_out, B, VEM_1);
  and and_1 (and_1_out, B, VEM_1);
  xor xor_2 (S, xor_1_out, VEM_1);
  and and_2 (and_2_out, or_1_out, A);
  or or_2 (VAI_1, and_2_out, and_1_out);
endmodule

module ADD_4 (
  input  [3:0] in_1,
  input  [3:0] in_2,
  input  VEM_1,
  output VAI_1,
  output [3:0] out_5
);

  wire add_1_2_vai_1, add_1_3_vai_1, add_1_4_vai_1;

  ADD_1 add_1_1 (.A(in_1[3]), .B(in_2[3]), .VEM_1(add_1_2_vai_1), .S(out_5[3]), .VAI_1(VAI_1));
  ADD_1 add_1_2 (.A(in_1[2]), .B(in_2[2]), .VEM_1(add_1_3_vai_1), .S(out_5[2]), .VAI_1(add_1_2_vai_1));
  ADD_1 add_1_3 (.A(in_1[1]), .B(in_2[1]), .VEM_1(add_1_4_vai_1), .S(out_5[1]), .VAI_1(add_1_3_vai_1));
  ADD_1 add_1_4 (.A(in_1[0]), .B(in_2[0]), .VEM_1(VEM_1), .S(out_5[0]), .VAI_1(add_1_4_vai_1));
endmodule

module Sub_1 (
  input  A,
  input  B,
  input  VEM_1,
  output S,
  output VAI_1
);

  wire and_1_out, and_2_out, not_1_out, or_1_out, xor_1_out;

  not not_1 (not_1_out, A);
  xor xor_1 (xor_1_out, A, B);
  or or_1 (or_1_out, B, VEM_1);
  and and_1 (and_1_out, B, VEM_1);
  xor xor_2 (S, xor_1_out, VEM_1);
  and and_2 (and_2_out, or_1_out, not_1_out);
  or or_2 (VAI_1, and_2_out, and_1_out);
endmodule

module Sub_4 (
  input  [3:0] in_1,
  input  [3:0] in_2,
  input  Vem_1,
  output Overflow,
  output [3:0] out_5
);

  wire sub_1_2_vai_1, sub_1_3_vai_1, sub_1_4_vai_1;

  Sub_1 sub_1_1 (.A(in_1[3]), .B(in_2[3]), .VEM_1(sub_1_2_vai_1), .S(out_5[3]), .VAI_1(Overflow));
  Sub_1 sub_1_2 (.A(in_1[2]), .B(in_2[2]), .VEM_1(sub_1_3_vai_1), .S(out_5[2]), .VAI_1(sub_1_2_vai_1));
  Sub_1 sub_1_3 (.A(in_1[1]), .B(in_2[1]), .VEM_1(sub_1_4_vai_1), .S(out_5[1]), .VAI_1(sub_1_3_vai_1));
  Sub_1 sub_1_4 (.A(in_1[0]), .B(in_2[0]), .VEM_1(Vem_1), .S(out_5[0]), .VAI_1(sub_1_4_vai_1));
endmodule
